# Fritzing sketch circuit_schematic (saved by Fritzing 0.8.5b)
breadboards: 1

parts:
  Part1 = Arduino Uno (Rev3)
  R1 = Resistor [tolerance=±5% resistance=220 package=THT]
  R2 = Resistor [tolerance=±5% resistance=220 package=THT]
  R3 = Resistor [tolerance=±5% resistance=220 package=THT]
  LED1 = RGB LED (com. anode, rbg) [package="5 mm [THT]"]
  J1 = Piezo Speaker
  R4 = Resistor [tolerance=±5% resistance=100 package=THT]

nets:
  N1: Part1.D8, R4.Pin_0
  N2: Part1.D9_PWM, R1.Pin_0
  N3: Part1.D10_PWM/SS, R2.Pin_0
  N4: Part1.D11_PWM/MOSI, R3.Pin_0
  N5: Part1.GND, LED1.red_cathode, J1.pin1
  N6: R1.Pin_1, LED1.common_anode
  N7: R2.Pin_1, LED1.blue_cathode
  N8: R3.Pin_1, LED1.green_cathode
  N9: J1.pin2, R4.Pin_1
